// Logisim project 1_bit.circ as structural Verilog: 1 circuit, main circuit main
module main (
  input  A,
  input  B,
  input  L,
  output S,
  output P
);

  wire and_1_out, and_2_out, and_3_out, and_4_out, and_5_out, and_6_out, and_7_out, not_1_out, not_2_out,
       not_3_out;

  not not_1 (not_1_out, A);
  not not_2 (not_2_out, B);
  not not_3 (not_3_out, L);
  and and_1 (and_1_out, not_1_out, not_2_out, L);
  and and_2 (and_2_out, A, not_2_out, not_3_out);
  or or_1 (S, and_1_out, and_2_out, and_3_out, and_4_out);
  and and_3 (and_3_out, A, B, L);
  and and_4 (and_4_out, not_1_out, B, not_3_out);
  and and_5 (and_5_out, A, B);
  or or_2 (P, and_5_out, and_6_out, and_7_out);
  and and_6 (and_6_out, B, L);
  and and_7 (and_7_out, A, L);
endmodule
