// Logisim project trigger.circ as structural Verilog: 1 circuit, main circuit main
module main (
  input  in_1,
  output [2:0] out_2
);

  wire and_1_out, and_2_out, clock_1_out;

  Clock clock_1 (.out(clock_1_out));
  and and_1 (and_1_out, in_1, out_2[0]);
  T_Flip_Flop t_ff_1 (.clk(clock_1_out), .T(in_1), .Q(out_2[0]));  // open: Qn, preset, reset, en
  T_Flip_Flop t_ff_2 (.clk(clock_1_out), .T(and_1_out), .Q(out_2[1]));  // open: Qn, preset, reset, en
  T_Flip_Flop t_ff_3 (.clk(clock_1_out), .T(and_2_out), .Q(out_2[2]));  // open: Qn, preset, reset, en
  and and_2 (and_2_out, in_1, out_2[1], out_2[0]);
endmodule
